# Fritzing sketch V1-PCB (saved by Fritzing 0.9.5d)
circuit board: 17cm x 10cm
breadboards: 1

parts:
  Raspberry_Pi = Raspberry Pi 3 [part_number=RPI-3A+]
  S1 = Momentary Switch [package=tactile-pth]
  S3 = Momentary Switch [package=tactile-pth]
  S4 = Momentary Switch [package=tactile-pth]
  S5 = Momentary Switch [package=tactile-pth]
  S6 = Momentary Switch [package=tactile-pth]
  S7 = Momentary Switch [package=tactile-pth]
  S8 = Momentary Switch [package=tactile-pth]
  S9 = Momentary Switch [package=tactile-pth]
  S11 = Momentary Switch [package=tactile-pth]
  S12 = Momentary Switch [package=tactile-pth]
  S13 = Momentary Switch [package=tactile-pth]
  S14 = Momentary Switch [package=tactile-pth]
  S15 = Momentary Switch [package=tactile-pth]
  S16 = Momentary Switch [package=tactile-pth]
  S17 = Momentary Switch [package=tactile-pth]
  S18 = Momentary Switch [package=tactile-pth]
  S19 = Momentary Switch [package=tactile-pth]
  S20 = Momentary Switch [package=tactile-pth]
  S21 = Momentary Switch [package=tactile-pth]
  S22 = Momentary Switch [package=tactile-pth]
  S23 = Momentary Switch [package=tactile-pth]
  S24 = Momentary Switch [package=tactile-pth]
  S26 = Momentary Switch [package=tactile-pth]
  S27 = Momentary Switch [package=tactile-pth]
  S28 = Momentary Switch [package=tactile-pth]
  S29 = Momentary Switch [package=tactile-pth]
  S30 = Momentary Switch [package=tactile-pth]
  RE1 = Rotary Encoder [package=THT]  # not connected
  RE2 = Rotary Encoder [package=THT]  # not connected
  RE3 = Rotary Encoder [package=THT]  # not connected
  S31 = Momentary Switch [package=tactile-pth]
  S32 = Momentary Switch [package=tactile-pth]
  S33 = Momentary Switch [package=tactile-pth]
  S34 = Momentary Switch [package=tactile-pth]
  S35 = Momentary Switch [package=tactile-pth]
  S36 = Momentary Switch [package=tactile-pth]
  S37 = Momentary Switch [package=tactile-pth]
  S25 = Momentary Switch [package=tactile-pth]
  J1 = Camdenboss CTB0158-7 [part_number=CTB0158-7 package=THT]  # not connected
  D1 = Diode [package=diode-1n4148]
  D2 = Diode [package=diode-1n4148]
  D3 = Diode [package=diode-1n4148]
  D4 = Diode [package=diode-1n4148]
  D5 = Diode [package=diode-1n4148]
  D6 = Diode [package=diode-1n4148]
  D7 = Diode [package=diode-1n4148]
  D8 = Diode [package=diode-1n4148]
  D9 = Diode [package=diode-1n4148]
  D10 = Diode [package=diode-1n4148]
  D11 = Diode [package=diode-1n4148]
  D12 = Diode [package=diode-1n4148]
  D13 = Diode [package=diode-1n4148]
  D14 = Diode [package=diode-1n4148]
  D15 = Diode [package=diode-1n4148]
  D16 = Diode [package=diode-1n4148]
  D17 = Diode [package=diode-1n4148]
  D18 = Diode [package=diode-1n4148]
  D19 = Diode [package=diode-1n4148]
  D20 = Diode [package=diode-1n4148]
  D21 = Diode [package=diode-1n4148]
  D22 = Diode [package=diode-1n4148]
  D23 = Diode [package=diode-1n4148]
  D24 = Diode [package=diode-1n4148]
  D25 = Diode [package=diode-1n4148]
  D26 = Diode [package=diode-1n4148]
  D27 = Diode [package=diode-1n4148]
  D28 = Diode [package=diode-1n4148]
  D29 = Diode [package=diode-1n4148]
  D30 = Diode [package=diode-1n4148]
  D31 = Diode [package=diode-1n4148]
  D32 = Diode [package=diode-1n4148]
  D33 = Diode [package=diode-1n4148]
  D34 = Diode [package=diode-1n4148]
  D35 = Diode [package=diode-1n4148]
  D36 = Diode [package=diode-1n4148]
  D37 = Diode [package=diode-1n4148]
  R6 = Resistor [tolerance=±5% resistance=10k package=THT]
  R5 = Resistor [tolerance=±5% resistance=10k package=THT]
  R8 = Resistor [tolerance=±5% resistance=10k package=THT]
  R4 = Resistor [tolerance=±5% resistance=10k package=THT]
  R3 = Resistor [tolerance=±5% resistance=10k package=THT]
  R2 = Resistor [tolerance=±5% resistance=10k package=THT]
  R1 = Resistor [tolerance=±5% resistance=10k package=THT]
  R7 = Resistor [tolerance=±5% resistance=10k package=THT]
  S10 = Momentary Switch [package=tactile-pth]
  S2 = Momentary Switch [package=tactile-pth]

nets:
  N1: Raspberry_Pi.GPIO13, S8.3, S8.4, S16.3, S16.4, S24.3, S24.4, S32.3, S32.4, R8.Pin_1
  N2: Raspberry_Pi.GPIO19, S7.3, S7.4, S15.3, S15.4, S23.3, S23.4, S31.3, S31.4, R7.Pin_1
  N3: Raspberry_Pi.GPIO26, D33.C, D34.C, D35.C, D36.C, D37.C
  N4: Raspberry_Pi.GPIO21, D1.C, D2.C, D3.C, D4.C, D5.C, D6.C, D7.C, D8.C
  N5: Raspberry_Pi.GPIO20, D9.C, D10.C, D11.C, D12.C, D13.C, D14.C, D15.C, D16.C
  N6: Raspberry_Pi.GPIO16, D17.C, D18.C, D19.C, D20.C, D21.C, D22.C, D23.C, D24.C
  N7: Raspberry_Pi.GPIO12, D25.C, D26.C, D27.C, D28.C, D29.C, D30.C, D31.C, D32.C
  N8: Raspberry_Pi.GPIO25, S1.3, S1.4, S9.4, R1.Pin_1
  N9: Raspberry_Pi.GPIO24, S18.3, S18.4, S26.3, S26.4, S34.3, S34.4, R2.Pin_1, S10.3, S10.4, S2.3, S2.4
  N10: Raspberry_Pi.GPIO23, S3.3, S3.4, S11.3, S11.4, S19.3, S19.4, S27.3, S27.4, S35.3, S35.4, R3.Pin_1
  N11: Raspberry_Pi.GPIO18, S4.3, S4.4, S12.3, S12.4, S20.3, S20.4, S28.3, S28.4, S36.3, S36.4, R4.Pin_1
  N12: Raspberry_Pi.GPIO15, S5.3, S5.4, S13.3, S13.4, S21.3, S21.4, S29.3, S29.4, S37.3, S37.4, R5.Pin_1
  N13: Raspberry_Pi.GPIO14, S6.3, S6.4, S14.3, S14.4, S22.3, S22.4, S30.3, S30.4, R6.Pin_1
  N14: Raspberry_Pi.5V, R6.Pin_0, R5.Pin_0, R8.Pin_0, R4.Pin_0, R3.Pin_0, R2.Pin_0, R1.Pin_0, R7.Pin_0
  N15: S1.1, S1.2, D1.A
  N16: S3.1, S3.2, D3.A
  N17: S4.1, S4.2, D4.A
  N18: S5.1, S5.2, D5.A
  N19: S6.1, S6.2, D6.A
  N20: S7.1, S7.2, D7.A
  N21: S8.1, S8.2, D8.A
  N22: S9.1, S9.2, D9.A
  N23: S9.3, S17.4
  N24: S11.1, S11.2, D11.A
  N25: S12.1, S12.2, D12.A
  N26: S13.1, S13.2, D13.A
  N27: S14.1, S14.2, D14.A
  N28: S15.1, S15.2, D15.A
  N29: S16.1, S16.2, D16.A
  N30: S17.1, S17.2, D17.A
  N31: S17.3, S25.4
  N32: S18.1, S18.2, D18.A
  N33: S19.1, S19.2, D19.A
  N34: S20.1, S20.2, D20.A
  N35: S21.1, S21.2, D21.A
  N36: S22.1, S22.2, D22.A
  N37: S23.1, S23.2, D23.A
  N38: S24.1, S24.2, D24.A
  N39: S26.1, S26.2, D26.A
  N40: S27.1, S27.2, D27.A
  N41: S28.1, S28.2, D28.A
  N42: S29.1, S29.2, D29.A
  N43: S30.1, S30.2, D30.A
  N44: S31.1, S31.2, D31.A
  N45: S32.1, S32.2, D32.A
  N46: S33.1, S33.2, D33.A
  N47: S33.3, S33.4, S25.3
  N48: S34.1, S34.2, D34.A
  N49: S35.1, S35.2, D35.A
  N50: S36.1, S36.2, D36.A
  N51: S37.1, S37.2, D37.A
  N52: S25.1, S25.2, D25.A
  N53: D2.A, S2.1, S2.2
  N54: D10.A, S10.1, S10.2

notes:
  OP-P1 V1

custom parts:
  Rotary Encoder: Rotary Encoder from ALPSec11e with switch.
