# Fritzing sketch pcb (saved by Fritzing 0.9.5d)
circuit board: 8.3cm x 6.3cm
breadboards: 1

parts:
  Raspberry_Pi_1 = Raspberry Pi 3 [part_number=RPI-3-V1.2]
  MAIN_POWER = Camdenboss CTB0158-2 [part_number=CTB0158-2 package=THT]
  DISPLAY = Camdenboss CTB0158-6 [part_number=CTB0158-6 package=THT]
  POTENTIOMETER = Camdenboss CTB0158-3 [part_number=CTB0158-3 package=THT]
  ADC = MCP3008 [package=dil16]
  ROTARY_ENCODERS = Camdenboss CTB0158-12 [part_number=CTB0158-12 package=THT]
  KEYS = Camdenboss CTB0158-12 [part_number=CTB0158-12 package=THT]

nets (from the pcb view):
  N1: Raspberry_Pi_1.GPIO2, KEYS.pin12
  N2: Raspberry_Pi_1.GPIO3, DISPLAY.pin5
  N3: Raspberry_Pi_1.GPIO4, ROTARY_ENCODERS.pin2
  N4: Raspberry_Pi_1.GND, MAIN_POWER.pin1, DISPLAY.pin2, POTENTIOMETER.pin3, ADC.DGND, ADC.AGND, ROTARY_ENCODERS.pin11
  N5: Raspberry_Pi_1.GPIO17, ROTARY_ENCODERS.pin3
  N6: Raspberry_Pi_1.GPIO27, ROTARY_ENCODERS.pin4
  N7: Raspberry_Pi_1.GPIO22, DISPLAY.pin6
  N8: Raspberry_Pi_1.3V3, ROTARY_ENCODERS.pin5
  N9: Raspberry_Pi_1.GPIO10, DISPLAY.pin3
  N10: Raspberry_Pi_1.GPIO11, DISPLAY.pin4
  N11: Raspberry_Pi_1.ID_SD, ROTARY_ENCODERS.pin6
  N12: Raspberry_Pi_1.GPIO5, ROTARY_ENCODERS.pin7
  N13: Raspberry_Pi_1.GPIO6, ROTARY_ENCODERS.pin8
  N14: Raspberry_Pi_1.GPIO13, ROTARY_ENCODERS.pin9
  N15: Raspberry_Pi_1.GPIO19, ADC.Dout
  N16: Raspberry_Pi_1.GPIO26, ROTARY_ENCODERS.pin10
  N17: Raspberry_Pi_1.GPIO21, ADC.CLK
  N18: Raspberry_Pi_1.GPIO20, ADC.Din
  N19: Raspberry_Pi_1.GPIO16, ADC.CS/SHDN
  N20: Raspberry_Pi_1.GPIO12, KEYS.pin2
  N21: Raspberry_Pi_1.ID_SC, KEYS.pin3
  N22: Raspberry_Pi_1.GPIO7, KEYS.pin4
  N23: Raspberry_Pi_1.GPIO8, KEYS.pin5
  N24: Raspberry_Pi_1.GPIO25, KEYS.pin6
  N25: Raspberry_Pi_1.GPIO24, KEYS.pin7
  N26: Raspberry_Pi_1.GPIO23, KEYS.pin8
  N27: Raspberry_Pi_1.GPIO18, KEYS.pin9
  N28: Raspberry_Pi_1.GPIO15, KEYS.pin10
  N29: Raspberry_Pi_1.GPIO14, KEYS.pin11
  N30: Raspberry_Pi_1.5V, MAIN_POWER.pin2, DISPLAY.pin1, ROTARY_ENCODERS.pin12
  N31: POTENTIOMETER.pin1, ADC.VREF, ADC.VDD
  N32: POTENTIOMETER.pin2, ADC.CH0

notes:
  GND - VCC
  VCC
  GND-5V
  GND
  A B SW
  E1
  E2
  E3
