# Fritzing sketch schematics (saved by Fritzing 0.9.5d)
breadboards: 3

parts:
  Raspberry_Pi_1 = Raspberry Pi 3 [part_number=RPI-3-V1.2]
  ADC1 = MCP3008 [package=dil16]
  U1 = POT [package=alps_pot]
  U2 = POT [package=alps_pot]
  U3 = POT [package=alps_pot]
  U4 = POT [package=alps_pot]
  IC1 = MCP23017 I2C I/O Expander
  IC2 = MCP23017 I2C I/O Expander
  S1 = Momentary Switch [package=ksa_sealed_tac_switch]  # not connected
  S2 = Momentary Switch [package=ksa_sealed_tac_switch]  # not connected
  S3 = Momentary Switch [package=ksa_sealed_tac_switch]  # not connected
  S4 = Momentary Switch [package=ksa_sealed_tac_switch]  # not connected
  S5 = Momentary Switch [package=ksa_sealed_tac_switch]  # not connected
  S6 = Momentary Switch [package=ksa_sealed_tac_switch]  # not connected
  S7 = Momentary Switch [package=ksa_sealed_tac_switch]  # not connected
  S8 = Momentary Switch [package=ksa_sealed_tac_switch]  # not connected
  S9 = Momentary Switch [package=ksa_sealed_tac_switch]  # not connected
  S10 = Momentary Switch [package=ksa_sealed_tac_switch]  # not connected
  S11 = Momentary Switch [package=ksa_sealed_tac_switch]  # not connected
  S12 = Momentary Switch [package=ksa_sealed_tac_switch]  # not connected
  S13 = Momentary Switch [package=ksa_sealed_tac_switch]  # not connected
  S14 = Momentary Switch [package=ksa_sealed_tac_switch]  # not connected
  S15 = Momentary Switch [package=ksa_sealed_tac_switch]  # not connected
  S16 = Momentary Switch [package=ksa_sealed_tac_switch]  # not connected
  S17 = Momentary Switch [package=ksa_sealed_tac_switch]  # not connected
  S18 = Momentary Switch [package=ksa_sealed_tac_switch]  # not connected
  S19 = Momentary Switch [package=ksa_sealed_tac_switch]  # not connected
  S20 = Momentary Switch [package=ksa_sealed_tac_switch]  # not connected
  S21 = Momentary Switch [package=ksa_sealed_tac_switch]  # not connected
  S22 = Momentary Switch [package=ksa_sealed_tac_switch]  # not connected
  S23 = Momentary Switch [package=ksa_sealed_tac_switch]  # not connected
  S24 = Momentary Switch [package=ksa_sealed_tac_switch]  # not connected

nets:
  3V3: Raspberry_Pi_1.3v3, ADC1.VREF, ADC1.VDD
  N1: Raspberry_Pi_1.GPIO2, IC1.SDA, IC2.SDA
  N2: Raspberry_Pi_1.GPIO3, IC1.SCL, IC2.SCL
  N3: Raspberry_Pi_1.GPIO10, ADC1.Din
  N4: Raspberry_Pi_1.GPIO9, ADC1.Dout
  N5: Raspberry_Pi_1.GPIO11, ADC1.CLK
  N6: Raspberry_Pi_1.GPIO8, ADC1.CS/SHDN
  N7: Raspberry_Pi_1.GND, ADC1.DGND, ADC1.AGND
  5V: Raspberry_Pi_1.5V, IC1.VDD, IC1.RESET, IC2.VSS
  N8: ADC1.CH0, U1.E, U2.E, U3.E, U4.E
  N9: ADC1.CH1, U2.S
  N10: ADC1.CH2, U4.S
  N11: ADC1.CH3, U3.S
  N12: U1.A, U2.A, U3.A, U4.A
  N13: IC1.VSS, IC1.A0, IC1.A1, IC1.A2, IC2.NC#11

custom parts:
  MCP23017 I2C I/O Expander: The MCP23017 uses two i2c pins (these can be shared with other i2c devices), and in exchange gives you 16 general purpose pins. You can set each of 16 pins to be input, output, input with a pullup or open drain. There's even the ability to get an interrupt via an external pin when any of the inputs change so you don't have to keep polling the chip.
